// Logisim project lab05_DFlip_Flop.circ as structural Verilog: 6 circuits, main circuit main
module main (
  input  Reset,
  input  [2:0] Sel
);

  wire clk_out;
  wire [3:0] deocde_counter_1_decode, down_counter_1_down, jhonson_counter_1_jhonson, multiplexer_1_out,
       ring_counter_1_ring, up_counter_1_up;

  Clock sysclk ();  // open: out
  Clock clk (.out(clk_out));
  Up_Counter up_counter_1 (.clk(clk_out), .rst(Reset), .Up(up_counter_1_up));
  Down_counter down_counter_1 (.clk(clk_out), .Reset(Reset), .Down(down_counter_1_down));
  Deocde_counter deocde_counter_1 (.clk(clk_out), .Reset(Reset), .Decode(deocde_counter_1_decode));
  Ring_counter ring_counter_1 (.clk(clk_out), .Reset(Reset), .Ring(ring_counter_1_ring));
  Jhonson_counter jhonson_counter_1 (.clk(clk_out), .Reset(Reset), .Jhonson(jhonson_counter_1_jhonson));
  Multiplexer #(.select(3), .width(4)) multiplexer_1 (
    .in0(up_counter_1_up), .in1(down_counter_1_down), .in2(deocde_counter_1_decode),
    .in3(ring_counter_1_ring), .in4(jhonson_counter_1_jhonson), .out(multiplexer_1_out), .sel(Sel));  // open: in5, in6, in7
  // Probe on multiplexer_1_out
  Hex_Digit_Display hex_digit_display_1 (.value(multiplexer_1_out));  // open: dp
endmodule

module Up_Counter (
  input  clk,
  input  rst,
  output [3:0] Up
);

  wire d_ff_1_qn, d_ff_2_qn, d_ff_3_qn, d_ff_4_qn;

  D_Flip_Flop d_ff_1 (.D(d_ff_1_qn), .clk(clk), .Q(Up[0]), .Qn(d_ff_1_qn), .reset(rst));  // open: preset
  D_Flip_Flop d_ff_2 (.D(d_ff_2_qn), .clk(d_ff_1_qn), .Q(Up[1]), .Qn(d_ff_2_qn), .reset(rst));  // open: preset
  D_Flip_Flop d_ff_3 (.D(d_ff_3_qn), .clk(d_ff_2_qn), .Q(Up[2]), .Qn(d_ff_3_qn), .reset(rst));  // open: preset
  D_Flip_Flop d_ff_4 (.D(d_ff_4_qn), .clk(d_ff_3_qn), .Q(Up[3]), .Qn(d_ff_4_qn), .reset(rst));  // open: preset
endmodule

module Down_counter (
  input  clk,
  input  Reset,
  output [3:0] Down
);

  wire d_ff_1_qn, d_ff_2_qn, d_ff_3_qn, d_ff_4_qn;

  D_Flip_Flop d_ff_1 (.D(d_ff_1_qn), .clk(clk), .Q(Down[0]), .Qn(d_ff_1_qn), .preset(Reset));  // open: reset
  D_Flip_Flop d_ff_2 (.D(d_ff_2_qn), .clk(Down[0]), .Q(Down[1]), .Qn(d_ff_2_qn), .preset(Reset));  // open: reset
  D_Flip_Flop d_ff_3 (.D(d_ff_3_qn), .clk(Down[1]), .Q(Down[2]), .Qn(d_ff_3_qn), .preset(Reset));  // open: reset
  D_Flip_Flop d_ff_4 (.D(d_ff_4_qn), .clk(Down[2]), .Q(Down[3]), .Qn(d_ff_4_qn), .preset(Reset));  // open: reset
endmodule

module Deocde_counter (
  input  clk,
  input  Reset,
  output [3:0] Decode
);

  wire and_1_out, d_ff_1_qn, d_ff_2_qn, d_ff_3_qn, d_ff_4_qn, or_1_out;

  D_Flip_Flop d_ff_1 (.D(d_ff_1_qn), .clk(clk), .Q(Decode[0]), .Qn(d_ff_1_qn), .reset(or_1_out));  // open: preset
  or or_1 (or_1_out, Reset, and_1_out);
  D_Flip_Flop d_ff_2 (.D(d_ff_2_qn), .clk(d_ff_1_qn), .Q(Decode[1]), .Qn(d_ff_2_qn), .reset(or_1_out));  // open: preset
  D_Flip_Flop d_ff_3 (.D(d_ff_3_qn), .clk(d_ff_2_qn), .Q(Decode[2]), .Qn(d_ff_3_qn), .reset(or_1_out));  // open: preset
  D_Flip_Flop d_ff_4 (.D(d_ff_4_qn), .clk(d_ff_3_qn), .Q(Decode[3]), .Qn(d_ff_4_qn), .reset(or_1_out));  // open: preset
  and and_1 (and_1_out, Decode[1], Decode[3]);
endmodule

module Ring_counter (
  input  clk,
  input  Reset,
  output [3:0] Ring
);

  D_Flip_Flop d_ff_1 (.D(Ring[3]), .clk(clk), .Q(Ring[0]), .preset(Reset));  // open: Qn, reset
  D_Flip_Flop d_ff_2 (.D(Ring[0]), .clk(clk), .Q(Ring[1]), .reset(Reset));  // open: Qn, preset
  D_Flip_Flop d_ff_3 (.D(Ring[1]), .clk(clk), .Q(Ring[2]), .reset(Reset));  // open: Qn, preset
  D_Flip_Flop d_ff_4 (.D(Ring[2]), .clk(clk), .Q(Ring[3]), .reset(Reset));  // open: Qn, preset
endmodule

module Jhonson_counter (
  input  clk,
  input  Reset,
  output [3:0] Jhonson
);

  wire d_ff_4_qn;

  D_Flip_Flop d_ff_1 (.D(d_ff_4_qn), .clk(clk), .Q(Jhonson[0]), .preset(Reset));  // open: Qn, reset
  D_Flip_Flop d_ff_2 (.D(Jhonson[0]), .clk(clk), .Q(Jhonson[1]), .reset(Reset));  // open: Qn, preset
  D_Flip_Flop d_ff_3 (.D(Jhonson[1]), .clk(clk), .Q(Jhonson[2]), .reset(Reset));  // open: Qn, preset
  D_Flip_Flop d_ff_4 (.D(Jhonson[2]), .clk(clk), .Q(Jhonson[3]), .Qn(d_ff_4_qn), .reset(Reset));  // open: preset
endmodule
